// Logisim project _ALU_.circ as structural Verilog: 13 circuits, main circuit Half_Adder
module Half_Adder (
  input  A,
  input  B,
  output SUM,
  output CARRY
);

  xor xor_1 (SUM, A, B);
  and and_1 (CARRY, B, A);
endmodule

module Full_Adder (
  input  A,
  input  B,
  input  Cin,
  output Cout,
  output SUM
);

  wire half_adder_1_carry, half_adder_1_sum, half_adder_2_carry;

  Half_Adder half_adder_1 (.A(A), .B(B), .SUM(half_adder_1_sum), .CARRY(half_adder_1_carry));
  Half_Adder half_adder_2 (.A(half_adder_1_sum), .B(Cin), .SUM(SUM), .CARRY(half_adder_2_carry));
  or or_1 (Cout, half_adder_1_carry, half_adder_2_carry);
endmodule

module Ripple_Carry_Adder (
  input  A0,
  input  B0,
  input  Cin,
  input  A1,
  input  B1,
  input  A2,
  input  B2,
  input  A3,
  input  B3,
  output S0,
  output S1,
  output S2,
  output S3,
  output Cout
);

  wire full_adder_1_cout, full_adder_2_cout, full_adder_3_cout;

  Full_Adder full_adder_1 (.A(A0), .B(B0), .Cin(Cin), .Cout(full_adder_1_cout), .SUM(S0));
  Full_Adder full_adder_2 (.A(A1), .B(B1), .Cin(full_adder_1_cout), .Cout(full_adder_2_cout), .SUM(S1));
  Full_Adder full_adder_3 (.A(A2), .B(B2), .Cin(full_adder_2_cout), .Cout(full_adder_3_cout), .SUM(S2));
  Full_Adder full_adder_4 (.A(A3), .B(B3), .Cin(full_adder_3_cout), .Cout(Cout), .SUM(S3));
endmodule

module B_Input_Logic_1bit (
  input  B_in,
  input  S0,
  input  S1,
  output B_out
);

  wire and_1_out, and_2_out, xor_1_out, xor_2_out;

  xor xor_1 (xor_1_out, B_in, S1);
  xor xor_2 (xor_2_out, S1, S0);
  and and_1 (and_1_out, S1, S0);
  and and_2 (and_2_out, xor_1_out, xor_2_out);
  or or_1 (B_out, and_2_out, and_1_out);
endmodule

module B_input_Logic_nbits (
  input  S0,
  input  S1,
  input  B0,
  input  B1,
  input  B2,
  input  B3,
  output Y0,
  output Y1,
  output Y2,
  output Y3
);

  B_Input_Logic_1bit b_input_logic_1bit_1 (.B_in(B0), .S0(S0), .S1(S1), .B_out(Y0));
  B_Input_Logic_1bit b_input_logic_1bit_2 (.B_in(B1), .S0(S0), .S1(S1), .B_out(Y1));
  B_Input_Logic_1bit b_input_logic_1bit_3 (.B_in(B2), .S0(S0), .S1(S1), .B_out(Y2));
  B_Input_Logic_1bit b_input_logic_1bit_4 (.B_in(B3), .S0(S0), .S1(S1), .B_out(Y3));
endmodule

module Arithmetic_Unit_1bit (
  input  C_in,
  input  A,
  input  B,
  input  S0,
  input  S1,
  output C_out,
  output SUM
);

  wire b_input_logic_1bit_1_b_out;

  B_Input_Logic_1bit b_input_logic_1bit_1 (.B_in(B), .S0(S0), .S1(S1), .B_out(b_input_logic_1bit_1_b_out));
  Full_Adder full_adder_1 (.A(A), .B(b_input_logic_1bit_1_b_out), .Cin(C_in), .Cout(C_out), .SUM(SUM));
endmodule

module Arithmetic_Unit_nbits (
  input  S0,
  input  S1,
  input  C_in,
  input  A0,
  input  B0,
  input  A1,
  input  B1,
  input  A2,
  input  B2,
  input  A3,
  input  B3,
  output SUM0,
  output SUM1,
  output SUM2,
  output SUM3,
  output C_out
);

  wire arithmetic_unit_1bit_1_c_out, arithmetic_unit_1bit_2_c_out, arithmetic_unit_1bit_3_c_out;

  Arithmetic_Unit_1bit arithmetic_unit_1bit_1 (
    .C_in(C_in), .A(A0), .B(B0), .S0(S0), .S1(S1), .C_out(arithmetic_unit_1bit_1_c_out), .SUM(SUM0));
  Arithmetic_Unit_1bit arithmetic_unit_1bit_2 (
    .C_in(arithmetic_unit_1bit_1_c_out), .A(A1), .B(B1), .S0(S0), .S1(S1),
    .C_out(arithmetic_unit_1bit_2_c_out), .SUM(SUM1));
  Arithmetic_Unit_1bit arithmetic_unit_1bit_3 (
    .C_in(arithmetic_unit_1bit_2_c_out), .A(A2), .B(B2), .S0(S0), .S1(S1),
    .C_out(arithmetic_unit_1bit_3_c_out), .SUM(SUM2));
  Arithmetic_Unit_1bit arithmetic_unit_1bit_4 (
    .C_in(arithmetic_unit_1bit_3_c_out), .A(A3), .B(B3), .S0(S0), .S1(S1), .C_out(C_out), .SUM(SUM3));
endmodule

module Logical_Unit_1bit (
  input  A,
  input  B,
  input  S1,
  input  S0,
  output A_AND_B,
  output A_OR_B,
  output A_XOR_B,
  output NOT_A
);

  wire and_1_out, and_2_out, and_3_out, and_4_out, and_5_out, not_1_out, not_2_out, not_3_out, not_4_out,
       not_5_out, or_1_out, xor_1_out;

  not not_1 (not_1_out, S1);
  not not_2 (not_2_out, S0);
  not not_3 (not_3_out, S1);
  not not_4 (not_4_out, S0);
  and and_1 (and_1_out, not_1_out, not_2_out);
  and and_2 (and_2_out, B, A);
  and and_3 (and_3_out, not_3_out, S0);
  or or_1 (or_1_out, B, A);
  not not_5 (not_5_out, A);
  and and_4 (and_4_out, S1, not_4_out);
  xor xor_1 (xor_1_out, B, A);
  and and_5 (and_5_out, S1, S0);
  and and_6 (A_AND_B, and_1_out, and_2_out);
  and and_7 (A_OR_B, and_3_out, or_1_out);
  and and_8 (A_XOR_B, and_4_out, xor_1_out);
  and and_9 (NOT_A, and_5_out, not_5_out);
  Clock clock_1 ();  // open: out

  // Notes on the sheet:
  //   A: pull=up
  //   *S1 = 0,S2=1(It is an OR operation)
  //   *S1=0,S2,=0(It is a And Operation)
  //   *S1 = 1,S2=0(It is a XOR operation)
  //   *S1 = 1,S2 =1(It is a Not operation) 
endmodule

module Logical_Unit_nbits (
  input  S1,
  input  S0,
  input  A0,
  input  B0,
  input  A1,
  input  B1,
  input  A2,
  input  B2,
  input  A3,
  input  B3,
  output OUT_0,
  output OUT_1,
  output OUT_2,
  output OUT_3
);

  wire logical_unit_1bit_1_a_and_b, logical_unit_1bit_1_a_or_b, logical_unit_1bit_1_a_xor_b,
       logical_unit_1bit_1_not_a, logical_unit_1bit_2_a_and_b, logical_unit_1bit_2_a_or_b,
       logical_unit_1bit_2_a_xor_b, logical_unit_1bit_2_not_a, logical_unit_1bit_3_a_and_b,
       logical_unit_1bit_3_a_or_b, logical_unit_1bit_3_a_xor_b, logical_unit_1bit_3_not_a,
       logical_unit_1bit_4_a_and_b, logical_unit_1bit_4_a_or_b, logical_unit_1bit_4_a_xor_b,
       logical_unit_1bit_4_not_a, or_1_out, or_2_out, or_3_out, or_4_out, or_5_out, or_6_out, or_7_out,
       or_8_out;

  Logical_Unit_1bit logical_unit_1bit_1 (
    .A(A0), .B(B0), .S1(S1), .S0(S0), .A_AND_B(logical_unit_1bit_1_a_and_b),
    .A_OR_B(logical_unit_1bit_1_a_or_b), .A_XOR_B(logical_unit_1bit_1_a_xor_b),
    .NOT_A(logical_unit_1bit_1_not_a));
  Logical_Unit_1bit logical_unit_1bit_2 (
    .A(A1), .B(B1), .S1(S1), .S0(S0), .A_AND_B(logical_unit_1bit_2_a_and_b),
    .A_OR_B(logical_unit_1bit_2_a_or_b), .A_XOR_B(logical_unit_1bit_2_a_xor_b),
    .NOT_A(logical_unit_1bit_2_not_a));
  Logical_Unit_1bit logical_unit_1bit_3 (
    .A(A2), .B(B2), .S1(S1), .S0(S0), .A_AND_B(logical_unit_1bit_3_a_and_b),
    .A_OR_B(logical_unit_1bit_3_a_or_b), .A_XOR_B(logical_unit_1bit_3_a_xor_b),
    .NOT_A(logical_unit_1bit_3_not_a));
  Logical_Unit_1bit logical_unit_1bit_4 (
    .A(A3), .B(B3), .S1(S1), .S0(S0), .A_AND_B(logical_unit_1bit_4_a_and_b),
    .A_OR_B(logical_unit_1bit_4_a_or_b), .A_XOR_B(logical_unit_1bit_4_a_xor_b),
    .NOT_A(logical_unit_1bit_4_not_a));
  or or_1 (or_1_out, logical_unit_1bit_1_a_and_b, logical_unit_1bit_1_a_or_b);
  or or_2 (or_2_out, logical_unit_1bit_1_a_xor_b, logical_unit_1bit_1_not_a);
  or or_3 (or_3_out, logical_unit_1bit_2_a_and_b, logical_unit_1bit_2_a_or_b);
  or or_4 (or_4_out, logical_unit_1bit_3_a_and_b, logical_unit_1bit_3_a_or_b);
  or or_5 (or_5_out, logical_unit_1bit_3_a_xor_b, logical_unit_1bit_3_not_a);
  or or_6 (or_6_out, logical_unit_1bit_4_a_and_b, logical_unit_1bit_4_a_or_b);
  or or_7 (or_7_out, logical_unit_1bit_2_a_xor_b, logical_unit_1bit_2_not_a);
  or or_8 (or_8_out, logical_unit_1bit_4_a_xor_b, logical_unit_1bit_4_not_a);
  or or_9 (OUT_0, or_1_out, or_2_out);
  or or_10 (OUT_1, or_3_out, or_7_out);
  or or_11 (OUT_2, or_4_out, or_5_out);
  or or_12 (OUT_3, or_6_out, or_8_out);
endmodule

module Multiplexer_Two_to_One (
  input  AU,
  input  LU,
  input  SEL,
  output G
);

  wire and_1_out, and_2_out, not_1_out;

  not not_1 (not_1_out, SEL);
  and and_1 (and_1_out, not_1_out, AU);
  and and_2 (and_2_out, SEL, LU);
  or or_1 (G, and_1_out, and_2_out);
endmodule

module ALU_1bit (
  input  C_in,
  input  A,
  input  B,
  input  S0,
  input  S1,
  input  SEL,
  output C_out,
  output G
);

  wire arithmetic_unit_1bit_1_sum, logical_unit_1bit_1_a_and_b, logical_unit_1bit_1_a_or_b,
       logical_unit_1bit_1_a_xor_b, logical_unit_1bit_1_not_a, or_1_out, or_2_out, or_3_out;

  Arithmetic_Unit_1bit arithmetic_unit_1bit_1 (
    .C_in(C_in), .A(A), .B(B), .S0(S0), .S1(S1), .C_out(C_out), .SUM(arithmetic_unit_1bit_1_sum));
  Logical_Unit_1bit logical_unit_1bit_1 (
    .A(A), .B(B), .S1(S1), .S0(S0), .A_AND_B(logical_unit_1bit_1_a_and_b),
    .A_OR_B(logical_unit_1bit_1_a_or_b), .A_XOR_B(logical_unit_1bit_1_a_xor_b),
    .NOT_A(logical_unit_1bit_1_not_a));
  or or_1 (or_1_out, logical_unit_1bit_1_a_and_b, logical_unit_1bit_1_a_or_b);
  or or_2 (or_2_out, logical_unit_1bit_1_a_xor_b, logical_unit_1bit_1_not_a);
  or or_3 (or_3_out, or_1_out, or_2_out);
  Multiplexer_Two_to_One multiplexer_two_to_one_1 (.AU(arithmetic_unit_1bit_1_sum), .LU(or_3_out), .SEL(SEL), .G(G));
endmodule

module ALU_nbit (
  input  C_in,
  input  A3,
  input  A2,
  input  A1,
  input  A0,
  input  B3,
  input  B2,
  input  B1,
  input  B0,
  input  S0,
  input  S1,
  input  SEL,
  output G3,
  output G2,
  output G1,
  output G0,
  output C_out
);

  wire alu_1bit_1_c_out, alu_1bit_2_c_out, alu_1bit_3_c_out;

  ALU_1bit alu_1bit_1 (.C_in(C_in), .A(A0), .B(B0), .S0(S0), .S1(S1), .SEL(SEL), .C_out(alu_1bit_1_c_out), .G(G0));
  ALU_1bit alu_1bit_2 (
    .C_in(alu_1bit_1_c_out), .A(A1), .B(B1), .S0(S0), .S1(S1), .SEL(SEL), .C_out(alu_1bit_2_c_out), .G(G1));
  ALU_1bit alu_1bit_3 (
    .C_in(alu_1bit_2_c_out), .A(A2), .B(B2), .S0(S0), .S1(S1), .SEL(SEL), .C_out(alu_1bit_3_c_out), .G(G2));
  ALU_1bit alu_1bit_4 (.C_in(alu_1bit_3_c_out), .A(A3), .B(B3), .S0(S0), .S1(S1), .SEL(SEL), .C_out(C_out), .G(G3));
endmodule

module ALU_clk_for_chronogram (
  output C_out,
  output G
);

  wire A_out, arithmetic_unit_1bit_1_sum, B_out, C_in_out, logical_unit_1bit_1_a_and_b,
       logical_unit_1bit_1_a_or_b, logical_unit_1bit_1_a_xor_b, logical_unit_1bit_1_not_a, or_1_out,
       or_2_out, or_3_out, S0_out, S1_out, SEL_out;

  Clock #(.highDuration(2), .lowDuration(2)) A (.out(A_out));
  Clock B (.out(B_out));
  Clock #(.highDuration(32), .lowDuration(32)) C_in (.out(C_in_out));
  Clock #(.highDuration(4), .lowDuration(4)) S0 (.out(S0_out));
  Clock #(.highDuration(8), .lowDuration(8)) S1 (.out(S1_out));
  Arithmetic_Unit_1bit arithmetic_unit_1bit_1 (
    .C_in(C_in_out), .A(A_out), .B(B_out), .S0(S0_out), .S1(S1_out), .C_out(C_out),
    .SUM(arithmetic_unit_1bit_1_sum));
  Logical_Unit_1bit logical_unit_1bit_1 (
    .A(A_out), .B(B_out), .S1(S1_out), .S0(S0_out), .A_AND_B(logical_unit_1bit_1_a_and_b),
    .A_OR_B(logical_unit_1bit_1_a_or_b), .A_XOR_B(logical_unit_1bit_1_a_xor_b),
    .NOT_A(logical_unit_1bit_1_not_a));
  or or_1 (or_1_out, logical_unit_1bit_1_a_and_b, logical_unit_1bit_1_a_or_b);
  or or_2 (or_2_out, logical_unit_1bit_1_a_xor_b, logical_unit_1bit_1_not_a);
  Clock #(.highDuration(16), .lowDuration(16)) SEL (.out(SEL_out));
  or or_3 (or_3_out, or_1_out, or_2_out);
  Multiplexer_Two_to_One multiplexer_two_to_one_1 (
    .AU(arithmetic_unit_1bit_1_sum), .LU(or_3_out), .SEL(SEL_out), .G(G));
endmodule
